// Logisim project hack_computer.circ as structural Verilog
module ALU (
  input  [15:0] x,
  input  zx,
  input  nx,
  input  [15:0] y,
  input  zy,
  input  ny,
  input  f,
  input  no,
  output [15:0] ot,
  output ng,
  output zr
);

  wire bitfinder_1_found;
  wire [15:0] adder_1_out, and_1_out, multiplexer_1_out, multiplexer_2_out, multiplexer_3_out,
       multiplexer_4_out, multiplexer_5_out, not_1_out, not_2_out, not_3_out;

  Multiplexer #(.width(16)) multiplexer_1 (.in0(x), .in1({16{1'b0}}), .out(multiplexer_1_out), .sel(zx));
  Multiplexer #(.width(16)) multiplexer_2 (.in0(y), .in1({16{1'b0}}), .out(multiplexer_2_out), .sel(zy));
  assign not_1_out = ~multiplexer_1_out;  // NOT_Gate not_1, 16 bits wide
  Multiplexer #(.width(16)) multiplexer_3 (.in0(multiplexer_1_out), .in1(not_1_out), .out(multiplexer_3_out), .sel(nx));
  Multiplexer #(.width(16)) multiplexer_4 (.in0(multiplexer_2_out), .in1(not_2_out), .out(multiplexer_4_out), .sel(ny));
  assign not_2_out = ~multiplexer_2_out;  // NOT_Gate not_2, 16 bits wide
  assign and_1_out = multiplexer_3_out & multiplexer_4_out;  // AND_Gate and_1, 16 bits wide
  Adder #(.width(16)) adder_1 (.a(multiplexer_3_out), .b(multiplexer_4_out), .out(adder_1_out));  // open: cin, cout
  Multiplexer #(.width(16)) multiplexer_5 (.in0(and_1_out), .in1(adder_1_out), .out(multiplexer_5_out), .sel(f));
  Multiplexer #(.width(16)) multiplexer_6 (.in0(multiplexer_5_out), .in1(not_3_out), .out(ot), .sel(no));
  assign not_3_out = ~multiplexer_5_out;  // NOT_Gate not_3, 16 bits wide
  BitSelector #(.width(16)) bitselector_1 (.in(ot), .out(ng), .sel(4'b1110));
  BitFinder #(.width(16)) bitfinder_1 (.in(ot), .found(bitfinder_1_found));  // open: index
  not not_4 (zr, bitfinder_1_found);

  // Notes on the sheet:
  //   y: initial=0xa
endmodule

module CPU (
  input  [15:0] instruction,
  input  [15:0] inM,
  input  reset,
  output [15:0] outM,
  output ng,
  output zr,
  output [15:0] outpc
);

  wire [15:0] AReg_q, DReg_q, multiplexer_1_out, multiplexer_2_out;

  Multiplexer #(.width(16)) multiplexer_1 (
    .in0(outM), .in1(instruction), .out(multiplexer_1_out), .sel(instruction[15]));
  Register #(.width(16)) AReg (.D(multiplexer_1_out), .Q(AReg_q));  // open: en, clk, clr
  Register #(.width(16)) DReg (.D(outM), .Q(DReg_q));  // open: en, clk, clr
  Multiplexer #(.width(16)) multiplexer_2 (.in0(AReg_q), .in1(inM), .out(multiplexer_2_out), .sel(instruction[12]));
  PC pc_1 (.inpc(AReg_q), .reset(reset), .outpc(outpc));  // open: inc, load
  ALU alu_1 (
    .x(multiplexer_2_out), .zx(instruction[11]), .nx(instruction[10]), .y(DReg_q), .zy(instruction[9]),
    .ny(instruction[8]), .f(instruction[7]), .no(instruction[6]), .ot(outM), .ng(ng), .zr(zr));

  // Other names for the same wires on the sheet: a = instruction[12]

  // Notes on the sheet:
  //   inM
  //   outM
endmodule

module PC (
  input  inc,
  input  [15:0] inpc,
  input  load,
  input  reset,
  output [15:0] outpc
);

  wire [15:0] inc16_1_outinc, inOrLoadOrReset, multiplexer_1_out, multiplexer_2_out;

  Register #(.width(16)) register_1 (.D(inOrLoadOrReset), .Q(outpc));  // open: en, clk, clr
  Inc16 inc16_1 (.inInc(outpc), .outInc(inc16_1_outinc));
  Multiplexer #(.width(16)) multiplexer_1 (.in0({16{1'b0}}), .in1(inc16_1_outinc), .out(multiplexer_1_out), .sel(inc));
  Multiplexer #(.width(16)) multiplexer_2 (.in0(multiplexer_1_out), .in1(inpc), .out(multiplexer_2_out), .sel(load));
  Multiplexer #(.width(16)) multiplexer_3 (
    .in0(multiplexer_2_out), .in1({16{1'b0}}), .out(inOrLoadOrReset), .sel(reset));
endmodule

module Inc16 (
  input  [15:0] inInc,
  output [15:0] outInc
);

  Adder #(.width(16)) adder_1 (.a(inInc), .b(16'h1), .out(outInc));  // open: cin, cout
endmodule
